# Fritzing sketch Arduino energy meter (saved by Fritzing 0.9.2b)
breadboards: 1

parts:
  Part1 = Arduino Board Ethernet
  R1 = Photocell (LDR) [package=THT]
  R3 = Photocell (LDR) [package=THT]
  R4 = Resistor [tolerance=±5% resistance=200k package=THT]
  R5 = Resistor [tolerance=±5% resistance=200k package=THT]

nets:
  N1: Part1.D2_PWM, R3.pin_1, R4.Pin_0
  N2: Part1.D3_PWM, R1.pin_1, R5.Pin_0
  N3: Part1.5V, R1.pin_0, R3.pin_0
  N4: Part1.GND, R4.Pin_1, R5.Pin_1

notes:
  Sensor 1
  Sensor 2
